// Logisim project Smart_Home_Security (1).circ as structural Verilog: 1 circuit, main circuit main
module main (
  input  D,
  input  W,
  input  P,
  input  M
);

  wire and_1_out, not_1_out, or_1_out, or_2_out;

  or or_1 (or_1_out, D, W);
  not not_1 (not_1_out, P);
  and and_1 (and_1_out, or_1_out, not_1_out);
  or or_2 (or_2_out, and_1_out, M);
  LED led_1 (.in(or_2_out));

  // Notes on the sheet:
  //   ALARM
endmodule
